# Fritzing sketch Intro To LoRa (saved by Fritzing 0.9.3b)

parts:
  Part1 = Adafruit RFM9x LoRa Radio [part_number="Adafruit #3072 and #3073"]
  Part4 = Arduino Uno (Rev3)
  Part6 = FC-28 Soil Hygrometer Module
  Part7 = FC-28 Soil Hygrometer Module - Probe
  ANT1 = Antenna  # not connected
  U1 = LCD-16X2 [package=lcd-16x2]
  LCM1602_IIC3 = LCM1602 IIC [part_number="LCM1602 IIC" chip_label="LCM1602 IIC" package="DIP (Dual Inline) [THT]"]
  Part8 = Arduino Uno (Rev3)
  ANT3 = Antenna  # not connected
  Part9 = Adafruit RFM9x LoRa Radio [part_number="Adafruit #3072 and #3073"]
  DHT1 = DHT22 Humidity and Temperature Sensor

nets:
  VIN: Part1.VIN, Part4.3V3
  GND: Part1.GND, Part4.GND, Part6.GND, DHT1.GND
  N1: Part1.EN, Part4.D13/SCK
  N2: Part1.DIO0, Part4.D2
  N3: Part1.SCK, Part4.D12/MISO
  N4: Part1.MISO, Part4.D11_PWM/MOSI
  N5: Part1.MOSI, Part4.D10_PWM/SS
  N6: Part1.RST, Part4.D9_PWM
  N7: Part4.A0, Part6.AO
  N8: Part4.D3_PWM, DHT1.DATA
  5V: Part4.5V, Part6.VCC, DHT1.VDD
  N9: Part6.POS, Part7.POS
  N10: Part6.NEG, Part7.NEG
  VSS: U1.VSS, LCM1602_IIC3.VSS
  VDD: U1.VDD, LCM1602_IIC3.VDD
  N11: U1.VO, LCM1602_IIC3.V0
  N12: U1.RS, LCM1602_IIC3.RS
  N13: U1.R_W, LCM1602_IIC3.RW
  N14: U1.E, LCM1602_IIC3.E
  N15: U1.DB0, LCM1602_IIC3.D0
  N16: U1.DB1, LCM1602_IIC3.D1
  N17: U1.DB2, LCM1602_IIC3.D2
  N18: U1.DB3, LCM1602_IIC3.D3
  N19: U1.DB4, LCM1602_IIC3.D4
  N20: U1.DB5, LCM1602_IIC3.D5
  N21: U1.DB6, LCM1602_IIC3.D6
  N22: U1.DB7, LCM1602_IIC3.D7
  N23: U1.A, LCM1602_IIC3.A
  N24: U1.K, LCM1602_IIC3.K
  GND_2: LCM1602_IIC3.GND, Part8.GND, Part9.GND
  VCC: LCM1602_IIC3.VCC, Part8.5V
  N25: LCM1602_IIC3.SDA, Part8.A5/SCL
  N26: LCM1602_IIC3.SCL, Part8.A4/SDA
  N27: LCM1602_IIC3.LED_A, LCM1602_IIC3.LED_B
  N28: Part8.D9_PWM, Part9.RST
  N29: Part8.D10_PWM/SS, Part9.DIO4, Part9.MOSI
  N30: Part8.D11_PWM/MOSI, Part9.MISO
  N31: Part8.D12/MISO, Part9.SCK
  N32: Part8.D13/SCK, Part9.EN
  N33: Part8.D2, Part9.DIO0
  3V3: Part8.3V3, Part9.VIN

custom parts:
  Adafruit RFM9x LoRa Radio: Sending data over long distances is like magic, and now you can be a magician with this range of powerful and easy-to-use radio modules. Sure, sometimes you want to talk to a computer (a good time to use WiFi) or perhaps communicate with a Phone (choose Bluetooth Low Energy!) but what if you want to send data very far? Most WiFi, Bluetooth, Zigbee and other wireless chipsets use 2.4GHz, which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
  FC-28 Soil Hygrometer Module: The FC-28 is a soil hygrometer module that uses the Texas Instruments LM393 comparator chip to provide an analog measurement of soil humidity. The digital output is high when soil moisture is over a certain threshold, as determined by adjusting the potentiometer.
  FC-28 Soil Hygrometer Module - Probe: The FC-28 is a soil hygrometer module that uses the Texas Instruments LM393 comparator chip to provide an analog measurement of soil humidity.
  LCM1602 IIC: I2C-Module to use a 1602 or 2004 LCD on with the wire.h libory Serial LCD Modul
